// Logisim project encode_decimal_to_binary.circ as structural Verilog: 2 circuits, main circuit main
module main (
);

  // Buffer buffer_1 is placed but not wired
endmodule

module encode_dec_to_bin (
  input  _0,
  input  _1,
  input  _2,
  input  _3,
  input  _4,
  input  _5,
  input  _6,
  input  _7,
  input  _8,
  input  _9,
  output out_11,
  output out_12,
  output out_13,
  output out_14
);

  or or_1 (out_11, _9, _8);
  or or_2 (out_12, _7, _6, _5, _4);
  or or_3 (out_13, _7, _6, _3, _2);
  or or_4 (out_14, _9, _7, _5, _3, _1);

  // Notes on the sheet:
  //   enocder from deciaml to bindary
endmodule
